# Fritzing sketch TIP120 (saved by Fritzing 0.9.3b)
perfboards: 1
stripboards: 1

parts:
  Q2 = npn-Powertransistor [package="TO220 [THT]"]
  Q3 = npn-Powertransistor [package="TO220 [THT]"]
  J1 = Screw terminal - 2 pins [package=THT]  # not connected
  J2 = screw terminal, 2 pins  # not connected
  J3 = screw terminal, 2 pins
  J4 = female pin header, 2 pins [form="♀ (female)"]
  Nano1 = Arduino Nano v2.3
  J5 = female pin header, 2 pins [form="♀ (female)"]
  Componente1 = Bluetooth HC-05 Macho
  J6 = Screw terminal - 2 pins [package=THT]  # not connected

nets:
  N1: Q2.base, J4.pin2, Nano1.D10
  N2: Q3.base, J4.pin1, Nano1.D11
  N3: Q3.emitter, J3.pin1
  N4: Nano1.D1TX, Componente1.RXD
  N5: Nano1.D0RX, Componente1.TXD
  N6: Nano1.GND, J5.pin1
